// Logisim project fullAdder_8bits.circ as structural Verilog: 1 circuit, main circuit main
module main (
  input  Carry_In,
  input  [7:0] A,
  input  [7:0] B,
  output [7:0] out_4,
  output Carry_Out
);

  Adder adder_1 (.a(A), .b(B), .out(out_4), .cin(Carry_In), .cout(Carry_Out));
endmodule
