// Logisim project ula_8bits.circ as structural Verilog: 1 circuit, main circuit main
module main (
  input  Carry_in,
  input  [2:0] Opcode,
  input  [7:0] Input_A,
  input  [7:0] Input_B,
  input  in_5,
  input  in_6,
  output [7:0] Output,
  output out_8,
  output Carry_out
);

  wire [7:0] adder_1_out, and_1_out, nand_1_out, nor_1_out, not_1_out, or_1_out, subtractor_1_out, xor_1_out;

  Adder adder_1 (.a(Input_A), .b(Input_B), .out(adder_1_out), .cin(Carry_in), .cout(Carry_out));
  Subtractor subtractor_1 (.a(Input_A), .b(Input_B), .out(subtractor_1_out), .bin(Carry_in), .bout(Carry_out));
  assign and_1_out = Input_A & Input_B;  // AND_Gate and_1, 8 bits wide
  assign or_1_out = Input_A | Input_B;  // OR_Gate or_1, 8 bits wide
  assign not_1_out = ~Input_A;  // NOT_Gate not_1, 8 bits wide
  assign xor_1_out = Input_A ^ Input_B;  // XOR_Gate xor_1, 8 bits wide
  assign nand_1_out = ~(Input_A & Input_B);  // NAND_Gate nand_1, 8 bits wide
  assign nor_1_out = ~(Input_A | Input_B);  // NOR_Gate nor_1, 8 bits wide
  Multiplexer #(.select(3), .width(8), .enable("false")) multiplexer_1 (
    .in0(adder_1_out), .in1(subtractor_1_out), .in2(and_1_out), .in3(or_1_out), .in4(not_1_out),
    .in5(xor_1_out), .in6(nand_1_out), .in7(nor_1_out), .out(Output), .sel(Opcode));
  xor xor_2 (out_8, in_5, in_6);
endmodule
